# Fritzing sketch gun-controller-v2 (saved by Fritzing 0.9.3b)
circuit board: 2.91cm x 4.21cm

parts:
  LED_header = Header 12 [package=1x12_machine-pin-header_lock.004]
  Encoder_header = Header 4 [package=molex-1x4_lock]
  Arduino_pro_mini_3_3v = Arduino Pro Mini (3.3V)

nets:
  N1: LED_header.1, Arduino_pro_mini_3_3v.D2
  N2: LED_header.2, Arduino_pro_mini_3_3v.D3
  N3: LED_header.3, Arduino_pro_mini_3_3v.D4
  N4: LED_header.4, Arduino_pro_mini_3_3v.D5
  N5: LED_header.5, Arduino_pro_mini_3_3v.D6
  N6: LED_header.6, Arduino_pro_mini_3_3v.D7
  N7: LED_header.7, Arduino_pro_mini_3_3v.D8
  N8: LED_header.8, Arduino_pro_mini_3_3v.D9
  N9: LED_header.9, Arduino_pro_mini_3_3v.D10
  N10: LED_header.10, Arduino_pro_mini_3_3v.MOSI
  N11: LED_header.11, Arduino_pro_mini_3_3v.MISO
  N12: LED_header.12, Arduino_pro_mini_3_3v.SCK
  N13: Encoder_header.1, Arduino_pro_mini_3_3v.A0
  N14: Encoder_header.2, Arduino_pro_mini_3_3v.GND
  N15: Encoder_header.3, Arduino_pro_mini_3_3v.A1
  N16: Encoder_header.4, Arduino_pro_mini_3_3v.A2

notes:
  Gakkle Inc
  Props - Models - Toys
  Rick's Portal Gun v2
