# Fritzing sketch gun-controller-v3 (saved by Fritzing 0.9.3b)
circuit board: 4cm x 4.5cm

parts:
  LED_header = Header 12 [package=1x12_machine-pin-header_lock.004]
  Encoder = Header 4 [package=molex-1x4_lock]
  Arduino_pro_mini_3_3v = Arduino Pro Mini (3.3V)
  Q1 = TRANSISTOR_NPN [package=sot89]
  Q2 = TRANSISTOR_NPN [package=sot89]
  Q3 = TRANSISTOR_NPN [package=sot89]
  Q4 = TRANSISTOR_NPN [package=sot89]
  R1 = Resistor [tolerance=±5% resistance=220 package="1206 [SMD]"]
  R2 = Resistor [tolerance=±5% resistance=220 package="1206 [SMD]"]
  R3 = Resistor [tolerance=±5% resistance=220 package="1206 [SMD]"]
  R4 = Resistor [tolerance=±5% resistance=220 package="1206 [SMD]"]
  R5 = Resistor [tolerance=±5% resistance=220 package="1206 [SMD]"]
  R6 = Resistor [tolerance=±5% resistance=220 package="1206 [SMD]"]
  R7 = Resistor [tolerance=±5% resistance=220 package="1206 [SMD]"]
  R8 = Resistor [tolerance=±5% resistance=220 package="1206 [SMD]"]
  LED_-_Power = Header 4 [package=molex-1x4_lock]

nets:
  N1: LED_header.1, Q1.E
  N2: LED_header.2, Q2.E
  N3: LED_header.3, Q4.E
  N4: LED_header.4, Q3.E
  N5: LED_header.5, R1.Pin_0
  N6: LED_header.6, R2.Pin_0
  N7: LED_header.7, R3.Pin_0
  N8: LED_header.8, R4.Pin_0
  N9: LED_header.9, R5.Pin_0
  N10: LED_header.10, R6.Pin_0
  N11: LED_header.11, R7.Pin_0
  N12: LED_header.12, R8.Pin_0
  N13: Encoder.1, Arduino_pro_mini_3_3v.A0
  N14: Encoder.2, Arduino_pro_mini_3_3v.GND, Q1.C, Q2.C, Q3.C, Q4.C, LED_-_Power.2, LED_-_Power.4
  N15: Encoder.3, Arduino_pro_mini_3_3v.A1
  N16: Encoder.4, Arduino_pro_mini_3_3v.A2
  N17: Arduino_pro_mini_3_3v.VCC, LED_-_Power.1, LED_-_Power.3
  N18: Arduino_pro_mini_3_3v.SCK, R8.Pin_1
  N19: Arduino_pro_mini_3_3v.MISO, R7.Pin_1
  N20: Arduino_pro_mini_3_3v.MOSI, R6.Pin_1
  N21: Arduino_pro_mini_3_3v.D10, R5.Pin_1
  N22: Arduino_pro_mini_3_3v.D9, R4.Pin_1
  N23: Arduino_pro_mini_3_3v.D8, R3.Pin_1
  N24: Arduino_pro_mini_3_3v.D7, R2.Pin_1
  N25: Arduino_pro_mini_3_3v.D6, R1.Pin_1
  N26: Arduino_pro_mini_3_3v.D5, Q3.B
  N27: Arduino_pro_mini_3_3v.D4, Q4.B
  N28: Arduino_pro_mini_3_3v.D3, Q2.B
  N29: Arduino_pro_mini_3_3v.D2, Q1.B

notes:
  Gakkle Inc
  Props - Models - Toys
  Rick's Portal Gun v2
