# Fritzing sketch gun-controller-v4 (saved by Fritzing 0.9.3b)
circuit board: 4cm x 4.5cm

parts:
  LED_header = Header 12 [package=1x12_machine-pin-header_lock.004]
  Encoder = Header 4 [package=molex-1x4_lock]
  Q1 = TRANSISTOR_NPN [package=sot89]
  Q2 = TRANSISTOR_NPN [package=sot89]
  Q3 = TRANSISTOR_NPN [package=sot89]
  Q4 = TRANSISTOR_NPN [package=sot89]
  R1 = Resistor [tolerance=±5% resistance=220 package="1206 [SMD]"]
  R2 = Resistor [tolerance=±5% resistance=220 package="1206 [SMD]"]
  R3 = Resistor [tolerance=±5% resistance=220 package="1206 [SMD]"]
  R4 = Resistor [tolerance=±5% resistance=220 package="1206 [SMD]"]
  R5 = Resistor [tolerance=±5% resistance=220 package="1206 [SMD]"]
  R6 = Resistor [tolerance=±5% resistance=220 package="1206 [SMD]"]
  R7 = Resistor [tolerance=±5% resistance=220 package="1206 [SMD]"]
  R8 = Resistor [tolerance=±5% resistance=220 package="1206 [SMD]"]
  LED_-_Power = Header 4 [package=molex-1x4_lock]
  + = Pad [width=3.0733545478652795 height=3.9745584725536962 connect=center]
  - = Pad [width=3.0733545478652795 height=3.9745584725536962 connect=center]
  U1 = 74HC595 [package="DIP16 [THT]"]
  U2 = ATtiny44A-SSU [package=sop-14]

nets:
  N1: LED_header.1, Q1.E
  N2: LED_header.2, Q2.E
  N3: LED_header.3, Q4.E
  N4: LED_header.4, Q3.E
  N5: LED_header.5, R1.Pin_0
  N6: LED_header.6, R2.Pin_0
  N7: LED_header.7, R3.Pin_0
  N8: LED_header.8, R4.Pin_0
  N9: LED_header.9, R5.Pin_0
  N10: LED_header.10, R6.Pin_0
  N11: LED_header.11, R7.Pin_0
  N12: LED_header.12, R8.Pin_0
  N13: Encoder.2, Q2.C, LED_-_Power.2, LED_-_Power.4
  N14: Q1.C, Q3.C, Q4.C
  N15: R1.Pin_1, U1.Q0
  N16: R2.Pin_1, U1.Q1
  N17: R3.Pin_1, U1.Q2
  N18: R4.Pin_1, U1.Q3
  N19: R5.Pin_1, U1.Q4
  N20: R6.Pin_1, U1.Q5
  N21: R7.Pin_1, U1.Q6
  N22: R8.Pin_1, U1.Q7
  N23: LED_-_Power.1, LED_-_Power.3
  VCC: +.pad, U1.MR, U1.VCC, U2.VCC
  GND: -.pad, U1.GND, U1.OE, U2.GND
  N24: U1.SH_CP, U2.PB3
  N25: U1.ST_CP, U2.PB1
  N26: U1.DS, U2.PB0

notes:
  Gakkle Inc
  Props - Models - Toys
  Rick's Portal Gun v2

custom parts:
  ATtiny44A-SSU: http://www.atmel.com/Images/8183S.pdf
